# Fritzing sketch neopixel-colorpicker (saved by Fritzing 0.9.3b)
breadboards: 1

parts:
  Mod1 = Raspberry Pi Pico
  Part1 = LCD1602-I2C
  Part2 = ws2812b [package="smd 2812b"]
  Part3 = Thumb Joystick

nets:
  GND: Mod1.pin_3, Mod1.pin_8, Mod1.pin_13, Mod1.pin_18, Mod1.pin_23, Mod1.pin_28, Mod1.pin_33, Mod1.pin_38, Part1.GND, Part2.VSS, Part3.GND
  N1: Mod1.pin_14, Part1.SCL
  N2: Mod1.pin_15, Part1.SDA
  N3: Mod1.pin_29, Part2.DIN
  N4: Mod1.pin_31, Part3.SEL
  N5: Mod1.pin_32, Part3.VERT
  N6: Mod1.pin_34, Part3.HORZ
  N7: Mod1.pin_36, Part3.VCC
  VCC: Mod1.pin_40, Part1.VCC, Part2.VDD

custom parts:
  Raspberry Pi Pico: Raspberry Pi Pico. Based around the RP2040 microcontroller the Pico is a low cost microcontroller device bringing Raspberry Pi quality, cost, and easy of use to the microcontroller space. Jan 2021, Split part in to two versions: tht (this one) and SMD. This one will drill holes for a .1 in header in pcb to allow plugging in the module as well as providing pads to solder the module to the top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
  LCD1602-I2C: A standard character display, usually with 2x16 characters. Comes in many colors with LCM1602 IIC attached.
